// Logisim project CPUProto1.circ as structural Verilog: 7 circuits, main circuit One_Bit_ALU
module One_Bit_ALU (
  input  Subt,
  input  C_In,
  input  A,
  input  B,
  input  [2:0] Selector,
  input  Less,
  output Result,
  output C_Out,
  output Set
);

  wire and_1_out, nor_1_out, or_1_out, xor_1_out, xor_2_out;

  and and_1 (and_1_out, A, B);
  or or_1 (or_1_out, A, B);
  xor xor_1 (xor_1_out, A, B);
  nor nor_1 (nor_1_out, A, B);
  xor xor_2 (xor_2_out, B, Subt);
  Adder #(.width(1)) adder_1 (.a(A), .b(xor_2_out), .out(Set), .cin(C_In), .cout(C_Out));
  Multiplexer #(.select(3)) multiplexer_1 (
    .in0(and_1_out), .in1(or_1_out), .in2(xor_1_out), .in3(nor_1_out), .in4(Set), .in5(Less), .out(Result),
    .sel(Selector));  // open: in6, in7
endmodule

module ALU_Eight_From_One (
  input  [7:0] A,
  input  [2:0] Selector,
  input  Subt,
  input  [7:0] B,
  output [7:0] Result,
  output Zero
);

  wire one_bit_alu_1_c_out, one_bit_alu_2_c_out, one_bit_alu_3_c_out, one_bit_alu_4_c_out,
       one_bit_alu_5_c_out, one_bit_alu_6_c_out, one_bit_alu_7_c_out, one_bit_alu_8_set;

  One_Bit_ALU one_bit_alu_1 (
    .Subt(Subt), .C_In(Subt), .A(A[0]), .B(B[0]), .Selector(Selector), .Less(one_bit_alu_8_set),
    .Result(Result[0]), .C_Out(one_bit_alu_1_c_out));  // open: Set
  One_Bit_ALU one_bit_alu_2 (
    .Subt(Subt), .C_In(one_bit_alu_1_c_out), .A(A[1]), .B(B[1]), .Selector(Selector), .Less(1'b0),
    .Result(Result[1]), .C_Out(one_bit_alu_2_c_out));  // open: Set
  One_Bit_ALU one_bit_alu_3 (
    .Subt(Subt), .C_In(one_bit_alu_2_c_out), .A(A[2]), .B(B[2]), .Selector(Selector), .Less(1'b0),
    .Result(Result[2]), .C_Out(one_bit_alu_3_c_out));  // open: Set
  One_Bit_ALU one_bit_alu_4 (
    .Subt(Subt), .C_In(one_bit_alu_3_c_out), .A(A[3]), .B(B[3]), .Selector(Selector), .Less(1'b0),
    .Result(Result[3]), .C_Out(one_bit_alu_4_c_out));  // open: Set
  One_Bit_ALU one_bit_alu_5 (
    .Subt(Subt), .C_In(one_bit_alu_4_c_out), .A(A[4]), .B(B[4]), .Selector(Selector), .Less(1'b0),
    .Result(Result[4]), .C_Out(one_bit_alu_5_c_out));  // open: Set
  One_Bit_ALU one_bit_alu_6 (
    .Subt(Subt), .C_In(one_bit_alu_5_c_out), .A(A[5]), .B(B[5]), .Selector(Selector), .Less(1'b0),
    .Result(Result[5]), .C_Out(one_bit_alu_6_c_out));  // open: Set
  One_Bit_ALU one_bit_alu_7 (
    .Subt(Subt), .C_In(one_bit_alu_6_c_out), .A(A[6]), .B(B[6]), .Selector(Selector), .Less(1'b0),
    .Result(Result[6]), .C_Out(one_bit_alu_7_c_out));  // open: Set
  One_Bit_ALU one_bit_alu_8 (
    .Subt(Subt), .C_In(one_bit_alu_7_c_out), .A(A[7]), .B(B[7]), .Selector(Selector), .Less(1'b0),
    .Result(Result[7]), .Set(one_bit_alu_8_set));  // open: C_Out
  nor nor_1 (Zero, Result[0], Result[1], Result[2], Result[3], Result[4], Result[5], Result[6], Result[7]);

  // Notes on the sheet:
  //   Inputs
  //   Enable to Subtract Instead of add
  //   Select Operations: 100 = ADD
  //   End Result
  //   Final Result is 0
endmodule

module Control_Unit (
  input  in_1,
  input  [2:0] in_2,
  output out_3,
  output out_4,
  output out_5,
  output out_6,
  output out_7,
  output out_8,
  output out_9,
  output out_10
);

  Decoder #(.select(3)) decoder_1 (
    .out0(out_3), .out1(out_4), .out2(out_5), .out3(out_6), .out4(out_7), .out5(out_8), .out6(out_9),
    .out7(out_10), .sel(in_2), .en(in_1));

  // Notes on the sheet:
  //   3 - 8 Decoder
endmodule

module Four_Bit_ALU (
  input  [3:0] Subtract,
  input  Carry_In,
  input  [3:0] A,
  input  [3:0] B,
  input  [3:0] Selector,
  input  [3:0] C_In_Mult,
  input  [3:0] C_In_Div,
  output [3:0] Result,
  output Carry_Out,
  output [3:0] C_Out_Mult,
  output [3:0] C_Out_Div
);

  wire [3:0] adder_1_out, and_1_out, divider_1_out, multiplier_1_out, nor_1_out, or_1_out, xor_1_out;

  Multiplier #(.width(4)) multiplier_1 (.a(A), .b(B), .out(multiplier_1_out), .cin(C_In_Mult), .cout(C_Out_Mult));
  Divider #(.width(4)) divider_1 (.a(A), .b(B), .out(divider_1_out), .upper(C_In_Div), .rem(C_Out_Div));
  assign and_1_out = A & B;  // AND_Gate and_1, 4 bits wide
  assign or_1_out = A | B;  // OR_Gate or_1, 4 bits wide
  assign nor_1_out = ~(A | B);  // NOR_Gate nor_1, 4 bits wide
  assign xor_1_out = B ^ Subtract;  // XOR_Gate xor_1, 4 bits wide
  Adder #(.width(4)) adder_1 (.a(A), .b(xor_1_out), .out(adder_1_out), .cin(Carry_In), .cout(Carry_Out));
  Multiplexer #(.select(4), .width(4)) multiplexer_1 (
    .in0(and_1_out), .in1(or_1_out), .in2(nor_1_out), .in3(adder_1_out), .in4(multiplier_1_out),
    .in5(divider_1_out), .out(Result), .sel(Selector));  // open: in6, in7, in8, in9, in10, in11, in12, in13, in14, in15

  // Notes on the sheet:
  //   Instructions:
  //   1. AND
  //   2. OR
  //   3. NOR
  //   4. ADD
  //   5. SUBTRACT
  //   6. MULTIPLY
  //   7. DIVIDE
  //   4 BIT ALU
  //   Operations Selector:
  //   0000 = AND
  //   0001 = OR
  //   0010 = NOR
  //   0011 = ADD/SUBTRACT
  //   0100 = MULTIPLY
  //   0101 = DIVIDE
endmodule

module Eight_Bit_ALU (
  input  Carry_In,
  input  [3:0] Subtract,
  input  [3:0] Selector,
  input  [7:0] A,
  input  [7:0] B,
  output [7:0] Result,
  output Zero
);

  wire four_bit_alu_1_carry_out;
  wire [3:0] four_bit_alu_1_c_out_div, four_bit_alu_1_c_out_mult, nor_1_out;

  Four_Bit_ALU four_bit_alu_1 (
    .Subtract(Subtract), .Carry_In(Carry_In), .A(A[3:0]), .B(B[3:0]), .Selector(Selector),
    .Result(Result[3:0]), .Carry_Out(four_bit_alu_1_carry_out), .C_Out_Mult(four_bit_alu_1_c_out_mult),
    .C_Out_Div(four_bit_alu_1_c_out_div));  // open: C_In_Mult, C_In_Div
  Four_Bit_ALU four_bit_alu_2 (
    .Subtract(Subtract), .Carry_In(four_bit_alu_1_carry_out), .A(A[7:4]), .B(B[7:4]), .Selector(Selector),
    .C_In_Mult(four_bit_alu_1_c_out_mult), .C_In_Div(four_bit_alu_1_c_out_div), .Result(Result[7:4]));  // open: Carry_Out, C_Out_Mult, C_Out_Div
  assign nor_1_out = ~(Result[3:0] | Result[7:4]);  // NOR_Gate nor_1, 4 bits wide
  nor nor_2 (Zero, nor_1_out[0], nor_1_out[1], nor_1_out[2], nor_1_out[3]);

  // Notes on the sheet:
  //   Inputs
  //   AND Subtract 1111
  //   Enable Carry To Subtract
  //   8 Bit ALU
  //   Operations Selector:
  //   0000 = AND
  //   0001 = OR
  //   0010 = NOR
  //   0011 = ADD/SUBTRACT
  //   0100 = MULTIPLY
  //   0101 = DIVIDE
  //   Final Result
  //   Subtract Result is Zero?
endmodule

module CPU_MAIN (
  input  in_1,
  input  [3:0] in_2,
  input  [3:0] in_3,
  input  [7:0] in_4,
  input  [7:0] in_5
);

  wire bcd_to_7_segment_decoder_3_p1, binary_to_bcd_converter_1_p2, binary_to_bcd_converter_1_p4, clock_1_out;
  wire [7:0] eight_bit_alu_1_result;

  Clock clock_1 (.out(clock_1_out));
  Eight_Bit_ALU eight_bit_alu_1 (
    .Carry_In(in_1), .Subtract(in_2), .Selector(in_3), .A(in_4), .B(in_5), .Result(eight_bit_alu_1_result));  // open: Zero
  _7_Segment_Display u_7_segment_display_1 ();  // open: g, f, a, b, e, d, c, dp
  // BCD_to_7_Segment_decoder bcd_to_7_segment_decoder_1: pin names not known
  // Binary_to_BCD_converter #(.binvalue(8)) binary_to_bcd_converter_1: pin names not known; wires that end beside it: eight_bit_alu_1_result, binary_to_bcd_converter_1_p2, binary_to_bcd_converter_1_p2, binary_to_bcd_converter_1_p4
  _7_Segment_Display u_7_segment_display_2 ();  // open: g, f, a, b, e, d, c, dp
  // BCD_to_7_Segment_decoder bcd_to_7_segment_decoder_2: pin names not known; wires that end beside it: binary_to_bcd_converter_1_p4
  _7_Segment_Display u_7_segment_display_3 ();  // open: g, f, a, b, e, d, c, dp
  // BCD_to_7_Segment_decoder bcd_to_7_segment_decoder_3: pin names not known; wires that end beside it: bcd_to_7_segment_decoder_3_p1, bcd_to_7_segment_decoder_3_p1

  // Notes on the sheet:
  //   CPU MAIN CIRCUIT
  //   0000 = AND
  //   0001 = OR
  //   0010 = NOR
  //   Operations Selector:
  //   0011 = ADD/SUBTRACT
  //   0100 = MULTIPLY
  //   0101 = DIVIDE
endmodule

module Registers (
  input  [7:0] RegVal,
  output [7:0] R0_Val,
  output [7:0] R1_Val,
  output [7:0] R2_Val,
  output [7:0] R3_Val
);

  wire clock_1_out;

  Register R0 (.D(RegVal), .Q(R0_Val), .clr(clock_1_out));  // open: en, clk
  Register R1 (.D(RegVal), .Q(R1_Val), .clr(clock_1_out));  // open: en, clk
  Register R2 (.D(RegVal), .Q(R2_Val), .clr(clock_1_out));  // open: en, clk
  Register R3 (.D(RegVal), .Q(R3_Val), .clr(clock_1_out));  // open: en, clk
  Clock clock_1 (.out(clock_1_out));
endmodule
